# Fritzing sketch bell-booster (saved by Fritzing 0.9.2b)
breadboards: 1

parts:
  L1 = Inductor [package="400 mil [THT]"]
  Q1 = Basic FET N-Channel [part_number=IRF710 package="TO220 [THT]"]
  Arduino_Uno = Arduino Uno (Rev3)
  L2 = Inductor [part_number="(bell coil)" package="400 mil [THT]"]
  C1 = Electrolytic Capacitor [capacitance=22µF voltage=0.4kV package="300 mil [THT, electrolytic]"]
  VCC1 = Battery block 9V [part_number=7.4V]
  D1 = Rectifier Diode [part_number=1N4007 package="300 mil [THT]"]
  DR1 = IC, DIP package, 8 pins [chip_label=DR1 part_number=TC4420]
  R1 = Resistor [tolerance=±5% resistance=100k package=THT]
  Q2 = NPN-Transistor [part_number=C33710 package="TO92 [THT]"]
  Q3 = Basic FET P-Channel [part_number=FU9310 package="TO220 [THT]"]
  R5 = Resistor [tolerance=±5% resistance=100k package=THT]
  R3 = Resistor [tolerance=±5% resistance=10k package=THT]
  Q4 = Basic FET N-Channel [part_number=IRF710 package="TO220 [THT]"]
  Q5 = Basic FET P-Channel [part_number=FU9310 package="TO220 [THT]"]
  Q6 = Basic FET N-Channel [part_number=IRF710 package="TO220 [THT]"]
  Q7 = NPN-Transistor [part_number=C33710 package="TO92 [THT]"]
  R4 = Resistor [tolerance=±5% resistance=10k package=THT]
  R2 = Resistor [tolerance=±5% resistance=100 package=THT]
  R6 = Resistor [tolerance=±5% resistance=100k package=THT]

nets:
  N1: L1.pin_0, Arduino_Uno.VIN, VCC1.+, DR1.pin1, DR1.pin8
  N2: L1.pin_1, Q1.drain, D1.anode
  N3: Q1.gate, R2.Pin_1
  N4: Q1.source, Arduino_Uno.GND, C1.-, VCC1.-, DR1.pin4, DR1.pin5, R1.Pin_0, Q2.E, Q4.source, Q6.source, Q7.E
  N5: Arduino_Uno.D8, DR1.pin2, R1.Pin_1
  N6: Arduino_Uno.D9_PWM, R3.Pin_0
  N7: Arduino_Uno.D10_PWM/SS, R4.Pin_0
  N8: L2.pin_0, Q3.source, Q4.drain, Q6.gate
  N9: L2.pin_1, Q4.gate, Q5.source, Q6.drain
  N10: C1.+, D1.cathode, Q3.drain, R5.Pin_1, Q5.drain, R6.Pin_1
  N11: DR1.pin6, DR1.pin7, R2.Pin_0
  N12: Q2.B, R3.Pin_1
  N13: Q2.C, Q3.gate, R5.Pin_0
  N14: Q5.gate, Q7.C, R6.Pin_0
  N15: Q7.B, R4.Pin_1

notes:
  4.2 kHz
  90%
  25 Hz
  50%
