# Fritzing sketch booster-driver (saved by Fritzing 0.9.2b)
breadboards: 1

parts:
  L1 = Inductor [inductance=2.2mH package="400 mil [THT]"]
  Q1 = Basic FET N-Channel [part_number=IRF710 package="TO220 [THT]"]
  Q2 = Basic FET N-Channel [part_number=IRF710 package="TO220 [THT]"]
  Arduino_Uno = Arduino Uno (Rev3)
  L2 = Inductor [package="400 mil [THT]"]
  C1 = Electrolytic Capacitor [capacitance=47µF package="300 mil [THT, electrolytic]"]
  D2 = Rectifier Diode [part_number=1N4007 package="Melf DO-213 AB [SMD]"]
  VCC1 = Battery block 9V [part_number=7.4V]
  D1 = Rectifier Diode [part_number=1N4007 package="300 mil [THT]"]
  R3 = Resistor [tolerance=±2% resistance=100 package=THT]
  DR1 = IC, DIP package, 8 pins [chip_label=DR1 part_number=TC4420]
  DR2 = IC, DIP package, 8 pins [chip_label=DR1 part_number=TC4420]
  R4 = Resistor [tolerance=±5% resistance=100 package=THT]
  R2 = Resistor [tolerance=±5% resistance=100k package=THT]
  R1 = Resistor [tolerance=±5% resistance=100k package=THT]
  R5 = Resistor [tolerance=±5% resistance=100k package=THT]
  R6 = Resistor [tolerance=±5% resistance=100k package=THT]

nets:
  N1: L1.pin_0, Arduino_Uno.VIN, VCC1.+, DR1.pin1, DR1.pin8, DR2.pin1, DR2.pin8
  N2: L1.pin_1, Q1.drain, D1.anode
  N3: Q1.gate, R3.Pin_1, R5.Pin_1
  N4: Q1.source, Q2.source, Arduino_Uno.GND, C1.-, VCC1.-, DR1.pin4, DR1.pin5, DR2.pin4, DR2.pin5, R2.Pin_0, R1.Pin_0, R5.Pin_0, R6.Pin_0
  N5: Q2.gate, R4.Pin_1, R6.Pin_1
  N6: Q2.drain, L2.pin_1, D2.anode
  N7: Arduino_Uno.D8, DR1.pin2, R1.Pin_1
  N8: Arduino_Uno.D9_PWM, DR2.pin2, R2.Pin_1
  N9: L2.pin_0, C1.+, D2.cathode, D1.cathode
  N10: R3.Pin_0, DR1.pin6, DR1.pin7
  N11: DR2.pin6, DR2.pin7, R4.Pin_0

notes:
  4 kHz
  92%
  25 Hz
  50%
