# Fritzing sketch booster-with-gen (saved by Fritzing 0.9.2b)
breadboards: 1

parts:
  Q1 = Basic FET N-Channel [part_number=IRF710 package="TO220 [THT]"]
  Arduino_Uno = Arduino Uno (Rev3)
  L1 = Inductor [package="400 mil [THT]"]
  C2 = Electrolytic Capacitor [capacitance=47µF package="300 mil [THT, electrolytic]"]
  D2 = Rectifier Diode [part_number=1N4007 package="Melf DO-213 AB [SMD]"]
  VCC1 = Battery block 9V [part_number=7.4V]
  D1 = Rectifier Diode [part_number=1N4007 package="300 mil [THT]"]
  DR1 = IC, DIP package, 8 pins [chip_label=DR1 part_number=TC4420]
  R2 = Resistor [tolerance=±0.5% resistance=100 package=THT]
  R1 = Resistor [tolerance=±5% resistance=100k package=THT]
  R3 = Resistor [tolerance=±5% resistance=100k package=THT]
  U1 = Transformer [package=transformer]
  C1 = Electrolytic Capacitor [capacitance=1µF voltage=50V package="100 mil [THT, electrolytic]"]
  R4 = Resistor [tolerance=±5% resistance=47 package=THT]
  Q2 = npn-Powertransistor [part_number=13007A package="TO220 [THT]"]

nets:
  N1: Q1.gate, R2.Pin_1, R3.Pin_1
  N2: Q1.drain, L1.pin_1, D2.anode
  N3: Q1.source, Arduino_Uno.GND, C2.-, VCC1.-, DR1.pin4, DR1.pin5, R1.Pin_0, R3.Pin_0, Q2.emitter
  N4: Arduino_Uno.D9_PWM, DR1.pin2, R1.Pin_1
  N5: Arduino_Uno.VIN, VCC1.+, DR1.pin1, DR1.pin8, U1.1, U1.4, R4.Pin_1
  N6: L1.pin_0, C2.+, D2.cathode, D1.cathode
  N7: D1.anode, U1.3, Q2.collector
  N8: DR1.pin6, DR1.pin7, R2.Pin_0
  N9: U1.2, C1.+
  N10: C1.-, R4.Pin_0, Q2.base

notes:
  25 Hz
  50%
