# Fritzing sketch telephone (saved by Fritzing 0.9.2b)
circuit board: 4cm x 3cm
circuit board: 3.99999cm x 2.99999cm
circuit board: 4cm x 3cm
breadboards: 2

parts:
  L1 = Inductor [package="400 mil [THT]"]
  Q1 = Basic FET N-Channel [part_number=IRF710 package="TO220 [THT]"]
  Arduino_Uno = Arduino Uno (Rev3)
  L2 = Inductor [part_number="(bell coil)" package="400 mil [THT]"]
  C3 = Electrolytic Capacitor [capacitance=22µF voltage=0.4kV package="300 mil [THT, electrolytic]"]
  VCC1 = Battery block 9V [part_number=7.4V]
  D1 = Rectifier Diode [part_number=1N4007 package="300 mil [THT]"]
  DR1 = IC, DIP package, 8 pins [chip_label=DR1 part_number=TC4420]
  Q2 = NPN-Transistor [part_number=KSP44 package="TO92 [THT]"]
  Q3 = Basic FET P-Channel [part_number=FU9310 package="TO220 [THT]"]
  R6 = Resistor [tolerance=±5% resistance=100k package=THT]
  R5 = Resistor [tolerance=±5% resistance=10k package=THT]
  Q5 = Basic FET P-Channel [part_number=FU9310 package="TO220 [THT]"]
  Q7 = NPN-Transistor [part_number=KSP44 package="TO92 [THT]"]
  R7 = Resistor [tolerance=±5% resistance=10k package=THT]
  R4 = Resistor [tolerance=±5% resistance=100 package=THT]
  R8 = Resistor [tolerance=±5% resistance=100k package=THT]
  R1 = Resistor [tolerance=±5% resistance=100k package=THT]
  Q4 = Basic FET N-Channel [part_number=IRF710 package="TO220 [THT]"]
  Q6 = Basic FET N-Channel [part_number=IRF710 package="TO220 [THT]"]
  U1 = 555 Timer [package="DIP8 [THT]"]
  C1 = Ceramic Capacitor [capacitance=100nF voltage=16V package="100 mil [THT, multilayer]"]
  R2 = Trimmer Potentiometer [maximum_resistance=10kΩ package=THT]
  R3 = Trimmer Potentiometer [maximum_resistance=10kΩ package=THT]
  C2 = Ceramic Capacitor [capacitance=10nF voltage=16V package="100 mil [THT, multilayer]"]
  Pad1 = Pad [width=10 height=17 connect=center]  # not connected

nets:
  N1: L1.pin_0, Arduino_Uno.VIN, VCC1.+, DR1.pin1, DR1.pin8
  N2: L1.pin_1, Q1.drain, D1.anode
  N3: Q1.gate, R4.Pin_1
  N4: Q1.source, Arduino_Uno.GND, C3.-, VCC1.-, DR1.pin4, DR1.pin5, Q2.E, Q7.E, R1.Pin_0, Q4.source, Q6.source, U1.Ground, C1.0, C2.0
  N5: Arduino_Uno.D10_PWM/SS, R5.Pin_0
  N6: Arduino_Uno.D11_PWM/MOSI, R7.Pin_0
  N7: Arduino_Uno.D12/MISO, DR1.pin2, R1.Pin_1
  N8: L2.pin_0, Q3.drain, Q4.drain, Q6.gate
  N9: L2.pin_1, Q5.drain, Q4.gate, Q6.drain
  N10: C3.+, D1.cathode, Q3.source, R6.Pin_1, Q5.source, R8.Pin_1
  N11: DR1.pin6, DR1.pin7, U1.Reset, U1.Vcc_Supply_Voltage, R2.leg2
  N12: Q2.B, R5.Pin_1
  N13: Q2.C, Q3.gate, R6.Pin_0
  N14: Q5.gate, Q7.C, R8.Pin_0
  N15: Q7.B, R7.Pin_1
  N16: R4.Pin_0, U1.Output
  N17: U1.Trigger, U1.Threshold, C1.1, R3.leg1, R3.wiper
  N18: U1.Control_Voltage, C2.1
  N19: U1.Discharge, R2.leg1, R2.wiper, R3.leg2

notes:
  DC-DC on/off
  25 Hz
  50%
  GND
  +60V
  A
  B
  +7.4V
  R2
  R3
  C
  D
  L2
