# Fritzing sketch telephone2 (saved by Fritzing 0.9.3b)
circuit board: 3.99999cm x 2.99999cm
circuit board: 3.99999cm x 2.99999cm
circuit board: 3.99999cm x 2.99999cm
breadboards: 2

parts:
  L1 = Inductor [package="400 mil [THT]"]
  Q1 = Basic FET N-Channel [part_number=IRF710 package="TO220 [THT]"]
  Arduino_Uno = Arduino Uno (Rev3)
  L2 = Inductor [part_number="(bell coil)" package="400 mil [THT]"]
  C3 = Electrolytic Capacitor [capacitance=22µF voltage=0.4kV package="300 mil [THT, electrolytic]"]
  VCC1 = Battery block 9V [part_number=7.4V]
  D1 = Rectifier Diode [part_number=1N4007 package="300 mil [THT]"]
  DR1 = IC, DIP package, 8 pins [chip_label=DR1 part_number=TC4420]
  Q2 = NPN-Transistor [part_number=KSP44 package="TO92 [THT]"]
  Q3 = Basic FET P-Channel [part_number=FU9310 package="TO220 [THT]"]
  R6 = Resistor [tolerance=±5% resistance=22k package=THT]
  R5 = Resistor [tolerance=±5% resistance=10k package=THT]
  Q5 = Basic FET P-Channel [part_number=FU9310 package="TO220 [THT]"]
  Q7 = NPN-Transistor [part_number=KSP44 package="TO92 [THT]"]
  R9 = Resistor [tolerance=±5% resistance=10k package=THT]
  R4 = Resistor [tolerance=±5% resistance=100 package=THT]
  R10 = Resistor [tolerance=±5% resistance=22k package=THT]
  R1 = Resistor [tolerance=±5% resistance=100k package=THT]
  Q4 = Basic FET N-Channel [part_number=IRF710 package="TO220 [THT]"]
  Q6 = Basic FET N-Channel [part_number=IRF710 package="TO220 [THT]"]
  U1 = 555 Timer [package="DIP8 [THT]"]
  C1 = Ceramic Capacitor [capacitance=100nF voltage=16V package="100 mil [THT, multilayer]"]
  R2 = Trimmer Potentiometer [maximum_resistance=10kΩ package=THT]
  R3 = Trimmer Potentiometer [maximum_resistance=10kΩ package=THT]
  C2 = Ceramic Capacitor [capacitance=10nF voltage=16V package="100 mil [THT, multilayer]"]
  Pad1 = Pad [width=10 height=17 connect=center]  # not connected
  S1 = Pushbutton [package="[THT]"]
  R9_2 = Resistor [tolerance=±5% resistance=100k package=THT]
  S2 = Pushbutton [package="[THT]"]
  R10_2 = Resistor [tolerance=±5% resistance=100k package=THT]
  S3 = Pushbutton [package="[THT]"]
  R11 = Resistor [tolerance=±5% resistance=100k package=THT]
  S4 = Pushbutton [package="[THT]"]
  R12 = Resistor [tolerance=±5% resistance=100k package=THT]
  S5 = Pushbutton [package="[THT]"]
  R13 = Resistor [tolerance=±5% resistance=100k package=THT]
  S6 = Pushbutton [package="[THT]"]
  R14 = Resistor [tolerance=±5% resistance=100k package=THT]
  MIC1 = Microphone
  J1 = Piezo Speaker
  LED1 = LED - 5mm [color="Blue (470nm)" part_number=BL-L513UBW package="5 mm [THT]"]
  R15 = Resistor [tolerance=±5% resistance=220 package=THT]
  R8 = Resistor [tolerance=±5% resistance=22k package=THT]
  R12_2 = Resistor [tolerance=±5% resistance=22k package=THT]
  R7 = Resistor [tolerance=±5% resistance=68k package=THT]
  R11_2 = Resistor [tolerance=±5% resistance=68k package=THT]

nets:
  N1: L1.pin_0, Arduino_Uno.VIN, VCC1.+, DR1.pin1, DR1.pin8
  N2: L1.pin_1, Q1.drain, D1.anode
  N3: Q1.gate, R4.Pin_1
  GND: Q1.source, Arduino_Uno.GND, C3.-, VCC1.-, DR1.pin4, DR1.pin5, R1.Pin_0, Q4.source, Q6.source, U1.Ground, C1.0, C2.0, S1.Pin_1, S1.Pin_2, S2.Pin_1, S2.Pin_2, S3.Pin_1, S3.Pin_2, S4.Pin_1, S4.Pin_2, S5.Pin_1, S5.Pin_2, S6.Pin_1, S6.Pin_2, LED1.cathode, R8.Pin_0, R12_2.Pin_0
  A0: Arduino_Uno.A0, S1.Pin_3, S1.Pin_4, R9_2.Pin_0
  A1: Arduino_Uno.A1, S2.Pin_3, S2.Pin_4, R10_2.Pin_0
  A2: Arduino_Uno.A2, S3.Pin_3, S3.Pin_4, R11.Pin_0
  A3: Arduino_Uno.A3, S4.Pin_3, S4.Pin_4, R12.Pin_0
  A4: Arduino_Uno.A4/SDA, S5.Pin_3, S5.Pin_4, R13.Pin_0
  A5: Arduino_Uno.A5/SCL, S6.Pin_3, S6.Pin_4, R14.Pin_0
  N4: Arduino_Uno.D10_PWM/SS, R5.Pin_0
  N5: Arduino_Uno.D11_PWM/MOSI, R9.Pin_0
  N6: Arduino_Uno.D12/MISO, DR1.pin2, R1.Pin_1
  D13: Arduino_Uno.D13/SCK, R15.Pin_1
  N7: Arduino_Uno.5V, R9_2.Pin_1, R10_2.Pin_1, R11.Pin_1, R12.Pin_1, R13.Pin_1, R14.Pin_1
  N8: L2.pin_0, Q5.drain, Q4.drain
  N9: L2.pin_1, Q3.drain, Q6.drain
  N10: C3.+, D1.cathode, Q3.source, R6.Pin_1, Q5.source, R10.Pin_1
  N11: DR1.pin6, DR1.pin7, U1.Reset, U1.Vcc_Supply_Voltage, R2.leg2
  N12: Q2.E, Q4.gate, R8.Pin_1
  N13: Q2.B, R5.Pin_1
  N14: Q2.C, R7.Pin_0
  N15: Q3.gate, R6.Pin_0, R7.Pin_1
  N16: Q5.gate, R10.Pin_0, R11_2.Pin_1
  N17: Q7.E, Q6.gate, R12_2.Pin_1
  N18: Q7.B, R9.Pin_1
  N19: Q7.C, R11_2.Pin_0
  N20: R4.Pin_0, U1.Output
  N21: U1.Trigger, U1.Threshold, C1.1, R3.leg1, R3.wiper
  N22: U1.Control_Voltage, C2.1
  N23: U1.Discharge, R2.leg1, R2.wiper, R3.leg2
  handset green: MIC1.pin1, J1.pin1
  handset red: MIC1.pin2
  handset white: J1.pin2
  N24: LED1.anode, R15.Pin_0

notes:
  C: DC-DC on/off
  25 Hz
  50%
  GND
  +60V
  A
  B
  +7.4V
  R2
  R3
  C
  D
  L2
  handset on/off
  rotary rolling
  rotary impulses
  * button
  # button
  + button
  A,B:
